// Logisim project lab2.circ as structural Verilog: 1 circuit, main circuit 四位二进制可逆计数器
module \四位二进制可逆计数器  (
  input  in_1,
  input  in_2,
  input  in_3,
  output out_4,
  output out_5,
  output out_6,
  output out_7
);

  wire B_qn, C_qn, clock_1_out, D_qn, nQA, QA, undriven;

  Clock clock_1 (.out(clock_1_out));
  D_Flip_Flop A (.clk(clock_1_out), .D(nQA), .Q(QA), .Qn(nQA), .reset(undriven));  // open: preset, en
  // AND_Gate and_1 has open pins: in0=in_1, out=open
  D_Flip_Flop B (.D(B_qn), .Qn(B_qn));  // open: clk, Q, preset, en, reset
  D_Flip_Flop C (.D(C_qn), .Qn(C_qn));  // open: clk, Q, preset, en, reset
  D_Flip_Flop D (.D(D_qn), .Qn(D_qn));  // open: clk, Q, preset, en, reset

  // Other names for the same wires on the sheet: CLR = in_2; CPD = in_3; CPU = in_1; SA = out_7; SB = out_6;
  //   SC = out_5; SD = out_4
endmodule
